# Fritzing sketch fritzing_sketch (saved by Fritzing 0.9.3b)
breadboards: 1

parts:
  Part1 = Arduino Uno (Rev3)
  Part2 = JY-MCU
  Part3 = SRF05 Ultrasonic Rangefinder

nets:
  N1: Part1.D0/RX, Part2.VCC
  N2: Part1.D1/TX, Part2.KEY
  N3: Part1.D7, Part3.Trig, Part3.Echo
  GND: Part1.GND, Part2.TX, Part3.GND
  VIN: Part1.VIN, Part2.RX, Part3.VCC

custom parts:
  JY-MCU: Description: The Bluetooth Mate is very similar to our BlueSMiRF modem, but it is designed specifically to be used with our Arduino Pros and LilyPad Arduinos. These modems work as a serial (RX/TX) pipe, and are a great wireless replacement for serial cables. Any serial stream from 9600 to 115200bps can be passed seamlessly from your computer to your target. Bluetooth Mate has the same pin out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
